# Fritzing sketch led_button_red_green (saved by Fritzing 0.9.0b)
breadboards: 1

parts:
  Raspberry_Pi_B_rev1 = Raspberry Pi B rev2
  S1 = Pushbutton [package="[THT]"]
  R1 = Resistor [tolerance=±5% resistance=220 package=THT]
  R2 = Resistor [tolerance=±5% resistance=220 package=THT]
  LED1 = LED - 5mm [color="Red (633nm)" package="5 mm [THT]"]
  LED2 = LED - 5mm [color="Green (570nm)" package="5 mm [THT]"]

nets:
  N1: Raspberry_Pi_B_rev1.3V3, R1.Pin_0, R2.Pin_0
  N2: Raspberry_Pi_B_rev1.GND, S1.Pin_3, S1.Pin_4
  N3: Raspberry_Pi_B_rev1.GPIO_17, LED2.cathode
  N4: Raspberry_Pi_B_rev1.GPIO_18, LED1.cathode
  N5: Raspberry_Pi_B_rev1.GPIO_27, S1.Pin_1, S1.Pin_2
  N6: R1.Pin_1, LED2.anode
  N7: R2.Pin_1, LED1.anode
